// Logisim project Final_Project.circ as structural Verilog: 12 circuits, main circuit Register File
module Register_File (
  input  [2:0] RA,
  input  [2:0] RB,
  input  [2:0] RW,
  input  [31:0] in_4,
  input  RegWrite,
  output [31:0] out_6,
  output [31:0] out_7
);

  wire and_1_out, and_2_out, and_3_out, and_4_out, and_5_out, and_6_out, and_7_out, Clock_out,
       decoder_1_out1, decoder_1_out2, decoder_1_out3, decoder_1_out4, decoder_1_out5, decoder_1_out6,
       decoder_1_out7, decoder_2_out0, decoder_2_out1, decoder_2_out2, decoder_2_out3, decoder_2_out4,
       decoder_2_out5, decoder_2_out6, decoder_2_out7, decoder_3_out0, decoder_3_out1, decoder_3_out2,
       decoder_3_out3, decoder_3_out4, decoder_3_out5, decoder_3_out6, decoder_3_out7;
  wire [31:0] R1, R2, R3, R4, R5, R6, R7;

  Clock Clock (.out(Clock_out));
  Decoder #(.select(3), .enable("false")) decoder_1 (
    .out1(decoder_1_out1), .out2(decoder_1_out2), .out3(decoder_1_out3), .out4(decoder_1_out4),
    .out5(decoder_1_out5), .out6(decoder_1_out6), .out7(decoder_1_out7), .sel(RW));  // open: out0
  and and_1 (and_1_out, decoder_1_out1, RegWrite);
  and and_2 (and_2_out, decoder_1_out2, RegWrite);
  and and_3 (and_3_out, decoder_1_out3, RegWrite);
  and and_4 (and_4_out, decoder_1_out4, RegWrite);
  and and_5 (and_5_out, decoder_1_out5, RegWrite);
  and and_6 (and_6_out, decoder_1_out6, RegWrite);
  and and_7 (and_7_out, decoder_1_out7, RegWrite);
  Register_part #(.width(32)) register_1 (.D(in_4), .en(and_1_out), .Q(R1), .clk(Clock_out));  // open: clr
  Register_part #(.width(32)) register_2 (.D(in_4), .en(and_2_out), .Q(R2), .clk(Clock_out));  // open: clr
  Register_part #(.width(32)) register_3 (.D(in_4), .en(and_3_out), .Q(R3), .clk(Clock_out));  // open: clr
  Register_part #(.width(32)) register_4 (.D(in_4), .en(and_4_out), .Q(R4), .clk(Clock_out));  // open: clr
  Register_part #(.width(32)) register_5 (.D(in_4), .en(and_5_out), .Q(R5), .clk(Clock_out));  // open: clr
  Register_part #(.width(32)) register_6 (.D(in_4), .en(and_6_out), .Q(R6), .clk(Clock_out));  // open: clr
  Register_part #(.width(32)) register_7 (.D(in_4), .en(and_7_out), .Q(R7), .clk(Clock_out));  // open: clr
  Decoder #(.select(3), .enable("false")) decoder_2 (
    .out0(decoder_2_out0), .out1(decoder_2_out1), .out2(decoder_2_out2), .out3(decoder_2_out3),
    .out4(decoder_2_out4), .out5(decoder_2_out5), .out6(decoder_2_out6), .out7(decoder_2_out7), .sel(RA));
  assign out_6 = decoder_2_out3 ? R3 : 32'bz;  // Controlled_Buffer controlled_buffer_1
  assign out_6 = decoder_2_out2 ? R2 : 32'bz;  // Controlled_Buffer controlled_buffer_2
  assign out_6 = decoder_2_out1 ? R1 : 32'bz;  // Controlled_Buffer controlled_buffer_3
  assign out_6 = decoder_2_out0 ? {32{1'b0}} : 32'bz;  // Controlled_Buffer controlled_buffer_4
  assign out_6 = decoder_2_out7 ? R7 : 32'bz;  // Controlled_Buffer controlled_buffer_5
  assign out_6 = decoder_2_out6 ? R6 : 32'bz;  // Controlled_Buffer controlled_buffer_6
  assign out_6 = decoder_2_out5 ? R5 : 32'bz;  // Controlled_Buffer controlled_buffer_7
  assign out_6 = decoder_2_out4 ? R4 : 32'bz;  // Controlled_Buffer controlled_buffer_8
  Decoder #(.select(3), .enable("false")) decoder_3 (
    .out0(decoder_3_out0), .out1(decoder_3_out1), .out2(decoder_3_out2), .out3(decoder_3_out3),
    .out4(decoder_3_out4), .out5(decoder_3_out5), .out6(decoder_3_out6), .out7(decoder_3_out7), .sel(RB));
  assign out_7 = decoder_3_out3 ? R3 : 32'bz;  // Controlled_Buffer controlled_buffer_9
  assign out_7 = decoder_3_out2 ? R2 : 32'bz;  // Controlled_Buffer controlled_buffer_10
  assign out_7 = decoder_3_out1 ? R1 : 32'bz;  // Controlled_Buffer controlled_buffer_11
  assign out_7 = decoder_3_out0 ? {32{1'b0}} : 32'bz;  // Controlled_Buffer controlled_buffer_12
  assign out_7 = decoder_3_out7 ? R7 : 32'bz;  // Controlled_Buffer controlled_buffer_13
  assign out_7 = decoder_3_out6 ? R6 : 32'bz;  // Controlled_Buffer controlled_buffer_14
  assign out_7 = decoder_3_out5 ? R5 : 32'bz;  // Controlled_Buffer controlled_buffer_15
  assign out_7 = decoder_3_out4 ? R4 : 32'bz;  // Controlled_Buffer controlled_buffer_16

  // Other names for the same wires on the sheet: BusW[31:0] = in_4
endmodule

module ALU_Register (
  input  [15:0] in_1,
  input  in_2
);

  wire [3:0] aluctrl_1_aluop;
  wire [31:0] alu_1_result, register_file_1_out_6, register_file_1_out_7;

  Register_File register_file_1 (
    .RA(in_1[7:5]), .RB(in_1[10:8]), .RW(in_1[13:11]), .in_4(alu_1_result), .RegWrite(in_2),
    .out_6(register_file_1_out_6), .out_7(register_file_1_out_7));
  ALUCtrl aluctrl_1 (.func(in_1[15:14]), .Op(in_1[4:0]), .ALUop(aluctrl_1_aluop));
  ALU alu_1 (
    .A(register_file_1_out_6), .B(register_file_1_out_7), .ALUop(aluctrl_1_aluop), .Result(alu_1_result));  // open: LT, zero

  // Other names for the same wires on the sheet: OP[4:0] = in_1[4:0]; Rs[2:0] = in_1[7:5]; Rt[2:0] = in_1[10:8];
  //   Rd[2:0] = in_1[13:11]; F[1:0] = in_1[15:14]
endmodule

module ALU (
  input  [31:0] A,
  input  [31:0] B,
  input  [3:0] ALUop,
  output [31:0] Result,
  output zero,
  output LT
);

  wire comparator_1_eq, comparator_1_lt, multiplexer_1_out;
  wire [31:0] adder_1_out, and_1_out, Arith, bit_extender_1_out, bit_extender_2_out, Logical, not_1_out,
       or_1_out, Shift, shifter_1_out, shifter_2_out, shifter_3_out, shifter_4_out, xor_1_out, xor_2_out;

  // Probe on A
  // Probe on B
  assign xor_1_out = A ^ bit_extender_1_out;  // XOR_Gate xor_1, 32 bits wide
  assign bit_extender_1_out = {{31{ALUop[0]}}, ALUop[0]};  // Bit_Extender bit_extender_1
  Comparator #(.width(32)) comparator_1 (.a(A), .b(B), .eq(comparator_1_eq), .lt(comparator_1_lt));  // open: gt
  assign and_1_out = B & A;  // AND_Gate and_1, 32 bits wide
  assign or_1_out = B | A;  // OR_Gate or_1, 32 bits wide
  assign xor_2_out = B ^ A;  // XOR_Gate xor_2, 32 bits wide
  Comparator #(.width(32)) comparator_2 (.a(A), .b(B), .eq(zero), .lt(LT));  // open: gt
  Shifter #(.width(32)) shifter_1 (.in(A), .\dist (B[4:0]), .out(shifter_1_out));
  Shifter #(.width(32), .shift("lr")) shifter_2 (.in(A), .\dist (B[4:0]), .out(shifter_2_out));
  Shifter #(.width(32), .shift("ar")) shifter_3 (.in(A), .\dist (B[4:0]), .out(shifter_3_out));
  Shifter #(.width(32), .shift("rr")) shifter_4 (.in(A), .\dist (B[4:0]), .out(shifter_4_out));
  Adder #(.width(32)) adder_1 (.a(B), .b(xor_1_out), .out(adder_1_out), .cin(ALUop[0]));  // open: cout
  Multiplexer #(.enable("false")) multiplexer_1 (
    .in0(comparator_1_eq), .in1(comparator_1_lt), .out(multiplexer_1_out), .sel(ALUop[0]));
  assign not_1_out = ~and_1_out;  // NOT_Gate not_1, 32 bits wide
  Multiplexer #(.select(2), .width(32), .enable("false")) multiplexer_2 (
    .in0(shifter_1_out), .in1(shifter_2_out), .in2(shifter_3_out), .in3(shifter_4_out), .out(Shift),
    .sel(ALUop[1:0]));
  Multiplexer #(.width(32), .enable("false")) multiplexer_3 (
    .in0(adder_1_out), .in1(bit_extender_2_out), .out(Arith), .sel(ALUop[1]));
  assign bit_extender_2_out = {{31{1'b0}}, multiplexer_1_out};  // Bit_Extender bit_extender_2
  Multiplexer #(.select(2), .width(32), .enable("false")) multiplexer_4 (
    .in0(and_1_out), .in1(not_1_out), .in2(or_1_out), .in3(xor_2_out), .out(Logical), .sel(ALUop[1:0]));
  // Probe on Result
  Multiplexer #(.select(2), .width(32), .enable("false")) multiplexer_5 (
    .in0(Logical), .in1(Arith), .in2(Shift), .in3(Arith), .out(Result), .sel(ALUop[3:2]));

  // Other names for the same wires on the sheet: Op0 = ALUop[0]; Op1 = ALUop[1]; Op2 = ALUop[2]; Op3 = ALUop[3]

  // Notes on the sheet:
  //   SLL
  //   SLR
  //   SRA
endmodule

module ALUCtrl (
  input  [4:0] Op,
  input  [1:0] func,
  output [3:0] ALUop
);

  wire and_1_out, and_2_out, and_3_out, and_4_out, not_1_out, not_2_out, not_3_out, or_3_out;
  wire [3:0] and_5_out;

  and and_1 (and_1_out, Op[4], Op[2]);
  not not_1 (not_1_out, and_1_out);
  and and_2 (and_2_out, Op[3], not_2_out);
  not not_2 (not_2_out, Op[2]);
  and and_3 (and_3_out, Op[2], Op[3]);
  and and_4 (and_4_out, Op[4], not_3_out);
  not not_3 (not_3_out, Op[2]);
  and and_5 (and_5_out[0], Op[0], not_1_out);
  or or_1 (and_5_out[2], and_2_out, Op[4]);
  or or_2 (and_5_out[3], and_3_out, and_4_out);
  Multiplexer #(.width(4), .enable("false")) multiplexer_1 (
    .in0({Op[1:0], func}), .in1({and_5_out[3:2], Op[1], and_5_out[0]}), .out(ALUop), .sel(or_3_out));
  or or_3 (or_3_out, Op[2], Op[3], Op[4]);
endmodule

module datapath (
  input  in_1
);

  wire clock_1_out, LT, main_control2_1_alusrc, main_control2_1_immext, main_control2_1_jmpadrs,
       main_control2_1_memrd, main_control2_1_memwr, main_control2_1_we, Zero;
  wire [1:0] f, main_control2_1_wbdata, main_control2_1_wsrc, pccntrl_1_pcsrc;
  wire [2:0] a, b, d, multiplexer_4_out;
  wire [3:0] aluctrl_1_aluop;
  wire [4:0] Op, Op2;
  wire [10:0] Imm_ex;
  wire [15:0] bit_extender_4_out, imm16, rom_1_data;
  wire [18:0] adder_1_out, adder_2_out, adder_3_out, bit_extender_1_out, bit_extender_2_out,
       multiplexer_1_out, multiplexer_2_out, pc_1_out_4;
  wire [31:0] Abus, alu_1_result, bit_extender_3_out, bit_extender_5_out, multiplexer_5_out,
       multiplexer_6_out, R1, R2, R3, R4, R5, R6, R7, ram_1_data, register_file_1_busb;

  Adder #(.width(19)) adder_1 (.a(19'h1), .b(pc_1_out_4), .out(adder_1_out));  // open: cin, cout
  // Probe on multiplexer_1_out
  Multiplexer #(.select(2), .width(19), .enable("false")) multiplexer_1 (
    .in0(adder_1_out), .in1(adder_2_out), .in2(Abus[18:0]), .out(multiplexer_1_out), .sel(pccntrl_1_pcsrc));  // open: in3
  PCcntrl pccntrl_1 (.PCsrc(pccntrl_1_pcsrc), .in_2(Op), .in_1(Zero), .LT(LT));
  Adder #(.width(19)) adder_2 (.a(multiplexer_2_out), .b(pc_1_out_4), .out(adder_2_out));  // open: cin, cout
  PC pc_1 (.in_1(multiplexer_1_out), .out_4(pc_1_out_4), .in_2(clock_1_out), .in_3(in_1));
  Multiplexer #(.width(19), .enable("false")) multiplexer_2 (
    .in0(bit_extender_2_out), .in1(bit_extender_1_out), .out(multiplexer_2_out), .sel(main_control2_1_jmpadrs));
  Clock clock_1 (.out(clock_1_out));
  Adder #(.width(19)) adder_3 (.a(19'h1), .b(pc_1_out_4), .out(adder_3_out));  // open: cin, cout
  assign bit_extender_1_out = {{8{a[2]}}, {a, b, d, f}};  // Bit_Extender bit_extender_1
  assign bit_extender_2_out = {{3{imm16[15]}}, imm16};  // Bit_Extender bit_extender_2
  ROM #(.addrWidth(19), .dataWidth(16)) rom_1 (.addr(pc_1_out_4), .data(rom_1_data));  // open: sel
  ROM #(.addrWidth(19), .dataWidth(16)) rom_2 (.addr(adder_3_out), .data({Op2, Imm_ex}));  // open: sel
  // Probe on R1
  // Probe on R2
  // Probe on R3
  // Probe on R4
  assign bit_extender_3_out = {{13{adder_1_out[18]}}, adder_1_out};  // Bit_Extender bit_extender_3
  // Probe on R5
  // Probe on R6
  // Probe on R7
  // Probe on Op
  Extractor extractor_1 (.Instruction(rom_1_data), .f(f), .d(d), .b(b), .a(a), .Op(Op));
  assign bit_extender_4_out = {{11{d[2]}}, {d, f}};  // Bit_Extender bit_extender_4
  Multiplexer #(.width(16), .enable("false")) multiplexer_3 (
    .in0(bit_extender_4_out), .in1({Imm_ex, d, f}), .out(imm16), .sel(main_control2_1_immext));
  Multiplexer #(.select(2), .width(3), .enable("false")) multiplexer_4 (
    .in0(b), .in1(d), .in2(3'b111), .out(multiplexer_4_out), .sel(main_control2_1_wsrc));  // open: in3
  Main_Control2 main_control2_1 (
    .in_1(Op), .Op2(Op2), .JmpAdrs(main_control2_1_jmpadrs), .Wsrc(main_control2_1_wsrc),
    .WE(main_control2_1_we), .ALUsrc(main_control2_1_alusrc), .MemRd(main_control2_1_memrd),
    .MemWr(main_control2_1_memwr), .WBdata(main_control2_1_wbdata), .ImmExt(main_control2_1_immext));
  assign bit_extender_5_out = {{16{imm16[15]}}, imm16};  // Bit_Extender bit_extender_5
  Register_File_2 register_file_1 (
    .BusW(multiplexer_6_out), .RW(multiplexer_4_out), .RegWrite(main_control2_1_we), .clck(clock_1_out),
    .BusA(Abus), .BusB(register_file_1_busb), .R3(R3), .R4(R4), .R5(R5), .R6(R6), .R7(R7), .R1(R1), .R2(R2),
    .RA(a), .RB(b));
  Multiplexer #(.width(32), .enable("false")) multiplexer_5 (
    .in0(bit_extender_5_out), .in1(register_file_1_busb), .out(multiplexer_5_out),
    .sel(main_control2_1_alusrc));
  ALUCtrl aluctrl_1 (.func(f), .Op(Op), .ALUop(aluctrl_1_aluop));
  ALU alu_1 (.A(Abus), .B(multiplexer_5_out), .ALUop(aluctrl_1_aluop), .Result(alu_1_result), .LT(LT), .zero(Zero));
  RAM #(.addrWidth(18), .dataWidth(32), .bus("separate")) ram_1 (
    .addr(alu_1_result[17:0]), .din(register_file_1_busb), .data(ram_1_data), .str(main_control2_1_memwr),
    .clk(clock_1_out), .ld(main_control2_1_memrd));  // open: sel, clr
  Multiplexer #(.select(2), .width(32), .enable("false")) multiplexer_6 (
    .in0(bit_extender_3_out), .in1(alu_1_result), .in2(ram_1_data), .out(multiplexer_6_out),
    .sel(main_control2_1_wbdata));  // open: in3

  // Other names for the same wires on the sheet: Imm5[4:0] = {d, f}; Imm11[10:0] = {a, b, d, f}

  // Notes on the sheet:
  //   contents of rom_1 (hex, n*v repeats v):
  //   4025 e802 4121 4125 d840
  //   contents of rom_2 (hex, n*v repeats v):
  //   4025 e802 4121 4125 d840
endmodule

module PC (
  input  [18:0] in_1,
  input  in_2,
  input  in_3,
  output [18:0] out_4
);

  wire [0:0] register_1_q;

  // Probe on in_1
  Register_part #(.width(20)) register_1 (
    .D({in_1, 1'b0}), .en(1'b1), .Q({out_4, register_1_q[0]}), .clk(in_2), .clr(in_3));
  // Probe on out_4
  // also tied to GND on the sheet: register_1_q[0]
endmodule

module Extractor (
  input  [15:0] Instruction,
  output [1:0] f,
  output [2:0] d,
  output [2:0] b,
  output [2:0] a,
  output [4:0] Op
);


  assign a = Instruction[10:8];
  assign b = Instruction[7:5];
  assign d = Instruction[4:2];
  assign f = Instruction[1:0];
  assign Op = Instruction[15:11];
endmodule

module PCcntrl (
  input  in_1,
  input  [4:0] in_2,
  input  LT,
  output [1:0] PCsrc
);

  wire and_1_out, and_2_out, and_3_out, and_4_out, and_5_out, BEQ, BLT, decoder_1_out0, decoder_1_out1,
       decoder_1_out4, decoder_1_out5, decoder_1_out6, decoder_1_out7, decoder_1_out8, decoder_1_out9,
       decoder_1_out10, decoder_1_out11, decoder_1_out12, decoder_1_out13, decoder_1_out14, decoder_1_out15,
       decoder_1_out17, decoder_1_out19, decoder_1_out20, decoder_1_out23, decoder_1_out28, decoder_1_out29,
       decoder_1_out30, not_1_out, not_2_out;

  and and_1 (and_1_out, decoder_1_out0, decoder_1_out1, decoder_1_out4, decoder_1_out5, decoder_1_out6, decoder_1_out7, decoder_1_out8, decoder_1_out9, decoder_1_out10, decoder_1_out11, decoder_1_out20, decoder_1_out12, decoder_1_out13, decoder_1_out14, decoder_1_out15, decoder_1_out30, decoder_1_out23);
  Decoder #(.select(5), .enable("false")) decoder_1 (
    .out0(decoder_1_out0), .out1(decoder_1_out1), .out4(decoder_1_out4), .out5(decoder_1_out5),
    .out6(decoder_1_out6), .out7(decoder_1_out7), .out8(decoder_1_out8), .out9(decoder_1_out9),
    .out10(decoder_1_out10), .out11(decoder_1_out11), .out12(decoder_1_out12), .out13(decoder_1_out13),
    .out14(decoder_1_out14), .out15(decoder_1_out15), .out16(BEQ), .out17(decoder_1_out17), .out18(BLT),
    .out19(decoder_1_out19), .out20(decoder_1_out20), .out23(decoder_1_out23), .out27(PCsrc[1]),
    .out28(decoder_1_out28), .out29(decoder_1_out29), .out30(decoder_1_out30), .sel(in_2));  // open: out2, out3, out21, out22, out24, out25, out26, out31
  and and_2 (and_2_out, BEQ, in_1);
  and and_3 (and_3_out, decoder_1_out17, not_1_out);
  not not_1 (not_1_out, in_1);
  and and_4 (and_4_out, decoder_1_out19, not_2_out);
  not not_2 (not_2_out, LT);
  or or_1 (PCsrc[0], and_1_out, and_2_out, and_3_out, and_4_out, decoder_1_out28, decoder_1_out29, and_5_out);
  and and_5 (and_5_out, BLT, LT);

  // Other names for the same wires on the sheet: OP[4:0] = in_2; branchJump = PCsrc[0]; TWO = PCsrc[1];
  //   ZeroFlag = in_1
endmodule

module Register (
  input  [31:0] Rin,
  input  WE,
  input  clock,
  output [31:0] Rout
);

  Register_part #(.width(32)) register_1 (.D(Rin), .en(WE), .Q(Rout), .clk(clock), .clr(1'b0));
endmodule

module Register_File_2 (
  input  [31:0] BusW,
  input  [2:0] RA,
  input  [2:0] RW,
  input  [2:0] RB,
  input  RegWrite,
  input  clck,
  output [31:0] R1,
  output [31:0] R2,
  output [31:0] R3,
  output [31:0] BusA,
  output [31:0] R4,
  output [31:0] R5,
  output [31:0] BusB,
  output [31:0] R6,
  output [31:0] R7
);

  wire and_1_out, and_2_out, and_3_out, and_4_out, and_5_out, and_6_out, and_7_out, decoder_1_out0,
       decoder_1_out1, decoder_1_out2, decoder_1_out3, decoder_1_out4, decoder_1_out5, decoder_1_out6,
       decoder_1_out7;

  Decoder #(.select(3), .enable("false")) decoder_1 (
    .out0(decoder_1_out0), .out1(decoder_1_out1), .out2(decoder_1_out2), .out3(decoder_1_out3),
    .out4(decoder_1_out4), .out5(decoder_1_out5), .out6(decoder_1_out6), .out7(decoder_1_out7), .sel(RW));
  and and_1 (and_1_out, RegWrite, decoder_1_out1);
  and and_2 (and_2_out, RegWrite, decoder_1_out2);
  and and_3 (and_3_out, RegWrite, decoder_1_out3);
  and and_4 (and_4_out, RegWrite, decoder_1_out4);
  and and_5 (and_5_out, RegWrite, decoder_1_out5);
  and and_6 (and_6_out, RegWrite, decoder_1_out6);
  and and_7 (and_7_out, RegWrite, decoder_1_out7);
  Register register_1 (.Rin(BusW), .WE(and_1_out), .clock(clck), .Rout(R1));
  Register register_2 (.Rin(BusW), .WE(and_2_out), .clock(clck), .Rout(R2));
  Register register_3 (.Rin(BusW), .WE(and_3_out), .clock(clck), .Rout(R3));
  Register register_4 (.Rin(BusW), .WE(and_4_out), .clock(clck), .Rout(R4));
  Register register_5 (.Rin(BusW), .WE(and_5_out), .clock(clck), .Rout(R5));
  Register register_6 (.Rin(BusW), .WE(and_6_out), .clock(clck), .Rout(R6));
  Register register_7 (.Rin(BusW), .WE(and_7_out), .clock(clck), .Rout(R7));
  Multiplexer #(.select(3), .width(32), .enable("false")) multiplexer_1 (
    .in0({32{1'b0}}), .in1(R1), .in2(R2), .in3(R3), .in4(R4), .in5(R5), .in6(R6), .in7(R7), .out(BusA),
    .sel(RA));
  Multiplexer #(.select(3), .width(32), .enable("false")) multiplexer_2 (
    .in0({32{1'b0}}), .in1(R1), .in2(R2), .in3(R3), .in4(R4), .in5(R5), .in6(R6), .in7(R7), .out(BusB),
    .sel(RB));

  // Other names for the same wires on the sheet: RegW = RegWrite; Rin[31:0] = BusW
endmodule

module Main_Control1 (
  input  [4:0] in_1,
  output ORI,
  output ANDI,
  output ADDI,
  output SEQI,
  output SLL,
  output SRA,
  output BEQ,
  output BLT,
  output LW,
  output JALR,
  output JAL,
  output CANDI,
  output XORI,
  output NADDI,
  output SLTI,
  output SRL,
  output ROR,
  output BNE,
  output BGE,
  output SW,
  output J,
  output IMM,
  output Rtype
);

  wire decoder_1_out0, decoder_1_out1;

  Decoder #(.select(5), .enable("false")) decoder_1 (
    .out0(decoder_1_out0), .out1(decoder_1_out1), .out4(ANDI), .out5(CANDI), .out6(ORI), .out7(XORI),
    .out8(ADDI), .out9(NADDI), .out10(SEQI), .out11(SLTI), .out12(SLL), .out13(SRL), .out14(SRA),
    .out15(ROR), .out16(BEQ), .out17(BNE), .out18(BLT), .out19(BGE), .out20(LW), .out21(SW), .out27(JALR),
    .out28(J), .out29(JAL), .out30(IMM), .sel(in_1));  // open: out2, out3, out22, out23, out24, out25, out26, out31
  or or_1 (Rtype, decoder_1_out0, decoder_1_out1);
endmodule

module Main_Control2 (
  input  [4:0] in_1,
  input  [4:0] Op2,
  output JmpAdrs,
  output [1:0] Wsrc,
  output WE,
  output ALUsrc,
  output MemRd,
  output MemWr,
  output [1:0] WBdata,
  output ImmExt
);

  wire and_1_out, main_control1_1_beq, main_control1_1_bge, main_control1_1_blt, main_control1_1_bne,
       main_control1_1_imm, main_control1_1_j, main_control1_1_jalr, main_control1_1_ror,
       main_control1_1_sll, main_control1_1_sra, main_control1_1_srl, not_3_out, or_2_out, or_3_out, or_5_out;

  Main_Control1 main_control1_1 (
    .in_1(in_1), .Rtype(Wsrc[0]), .SLL(main_control1_1_sll), .SRL(main_control1_1_srl),
    .SRA(main_control1_1_sra), .ROR(main_control1_1_ror), .BEQ(main_control1_1_beq),
    .BNE(main_control1_1_bne), .BLT(main_control1_1_blt), .BGE(main_control1_1_bge), .LW(MemRd), .SW(MemWr),
    .JALR(main_control1_1_jalr), .J(main_control1_1_j), .JAL(Wsrc[1]), .IMM(main_control1_1_imm));  // open: ANDI, CANDI, ORI, XORI, ADDI, NADDI, SEQI, SLTI
  or or_1 (ALUsrc, main_control1_1_beq, main_control1_1_bne, main_control1_1_blt, main_control1_1_bge, Wsrc[0]);
  or or_2 (or_2_out, main_control1_1_beq, main_control1_1_bne, main_control1_1_blt, main_control1_1_bge, MemWr, main_control1_1_j, main_control1_1_imm);
  not not_1 (WE, or_2_out);
  or or_3 (or_3_out, main_control1_1_jalr, MemRd);
  not not_2 (WBdata[0], or_3_out);
  or or_4 (JmpAdrs, main_control1_1_j, Wsrc[1]);
  or or_5 (or_5_out, main_control1_1_sll, main_control1_1_srl, Wsrc[0], main_control1_1_jalr, main_control1_1_j, Wsrc[1], main_control1_1_imm, main_control1_1_sra, main_control1_1_ror);
  not not_3 (not_3_out, or_5_out);
  and and_1 (and_1_out, Op2[4], Op2[3], Op2[2], Op2[1]);
  and and_2 (ImmExt, not_3_out, and_1_out);

  assign WBdata[1] = MemRd;
endmodule
